// Logisim project cpu.circ as structural Verilog: 4 circuits, main circuit ULA
module main (
  input  reset
);

  wire clk, cpu_1_out_8;
  wire [5:0] cpu_1_out_7;
  wire [7:0] cpu_1_out_5, cpu_1_out_6, ram_1_data, rom_1_data;

  Clock u_clk (.out(clk));
  CPU cpu_1 (
    .in_1(clk), .in_2(rom_1_data), .in_3(reset), .in_4(ram_1_data), .out_5(cpu_1_out_5), .out_6(cpu_1_out_6),
    .out_7(cpu_1_out_7), .out_8(cpu_1_out_8));
  ROM #(.addrWidth(6)) rom_1 (.addr(cpu_1_out_7), .data(rom_1_data));  // open: sel
  RAM #(.bus("separate")) ram_1 (
    .addr(cpu_1_out_6), .din(cpu_1_out_5), .data(ram_1_data), .str(cpu_1_out_8), .clk(clk), .ld(1'b1),
    .clr(reset));  // open: sel
endmodule

module ULA (
  input  [7:0] A,
  input  [7:0] B,
  input  [1:0] S,
  output [7:0] out_4,
  output out_5
);

  wire [7:0] adder_1_out, and_1_out, multiplier_1_out, or_1_out;

  Adder adder_1 (.a(A), .b(B), .out(adder_1_out));  // open: cin, cout
  Multiplier multiplier_1 (.a(A), .b(B), .out(multiplier_1_out));  // open: cin, cout
  assign and_1_out = A & B;  // AND_Gate and_1, 8 bits wide
  assign or_1_out = A | B;  // OR_Gate or_1, 8 bits wide
  Comparator #(.mode("unsigned")) comparator_1 (.a(A), .b(B), .gt(out_5));  // open: eq, lt
  Multiplexer #(.select(2), .width(8)) multiplexer_1 (
    .in0(adder_1_out), .in1(multiplier_1_out), .in2(and_1_out), .in3(or_1_out), .out(out_4), .sel(S));  // open: en
endmodule

module REGS (
  input  [1:0] adda,
  input  [1:0] addb,
  input  [7:0] \input ,
  input  clk,
  input  reset,
  input  en,
  output [7:0] outa,
  output [7:0] outb
);

  wire en0, en1, en2, en3;
  wire [7:0] q0, q1, q2, q3;

  Register register_1 (.D(\input ), .en(en0), .Q(q0), .clk(clk), .clr(reset));
  Register register_2 (.D(\input ), .en(en2), .Q(q2), .clk(clk), .clr(reset));
  Multiplexer #(.select(2), .width(8)) multiplexer_1 (
    .in0(q0), .in1(q1), .in2(q2), .in3(q3), .out(outb), .sel(addb));  // open: en
  Register register_3 (.D(\input ), .en(en1), .Q(q1), .clk(clk), .clr(reset));
  Register register_4 (.D(\input ), .en(en3), .Q(q3), .clk(clk), .clr(reset));
  Multiplexer #(.select(2), .width(8)) multiplexer_2 (
    .in0(q0), .in1(q1), .in2(q2), .in3(q3), .out(outa), .sel(adda));  // open: en
  Demultiplexer #(.select(2)) demultiplexer_1 (
    .out0(en0), .out1(en1), .out2(en2), .out3(en3), .in(en), .sel(adda));  // open: en
endmodule

module CPU (
  input  in_1,
  input  [7:0] in_2,
  input  in_3,
  input  [7:0] in_4,
  output [7:0] out_5,
  output [7:0] out_6,
  output [5:0] out_7,
  output out_8
);

  wire movecons, regen;
  wire [1:0] adda, addb, op;
  wire [5:0] nextline;
  wire [7:0] constant, multiplexer_1_out, outula, regs_1_outa, regs_1_outb;

  Register #(.width(6)) register_1 (.D(nextline), .en(in_1), .Q(out_7), .clk(in_1), .clr(in_3));
  Multiplexer #(.width(8)) multiplexer_1 (
    .in0(outula), .in1(constant), .out(multiplexer_1_out), .sel(movecons));  // open: en
  REGS regs_1 (
    .adda(adda), .addb(addb), .\input (multiplexer_1_out), .clk(in_1), .reset(in_3), .en(regen),
    .outa(regs_1_outa), .outb(regs_1_outb));
  Adder #(.width(6)) adder_1 (.a(out_7), .b(6'b000001), .out(nextline));  // open: cin, cout
  ULA ula_1 (.A(regs_1_outa), .B(regs_1_outb), .S(op), .out_4(outula));  // open: out_5

  // Other names for the same wires on the sheet: clk = in_1; memorin[7:0] = out_5; memoryadd[7:0] = out_6;
  //   memoryout[7:0] = in_4; opcode[7:0] = in_2; PC[5:0] = out_7; reset = in_3; str = out_8
endmodule
